// Logisim project datapath.circ as structural Verilog: 3 circuits, main circuit Datapath
module Datapath (
  input  Reset,
  input  Clear,
  input  Clear_2
);

  wire alu_1_zero, and_1_out, Clock_out, control_1_branch, control_1_escrevemem, control_1_escrevereg,
       control_1_jump, control_1_lemem, control_1_memparareg, control_1_origalu, control_1_regdst, not_1_out;
  wire [1:0] control_1_opalu;
  wire [3:0] alucontrol_1_operation;
  wire [4:0] instructiondecode_1_rd, instructiondecode_1_rs, instructiondecode_1_rt, multiplexer_1_out;
  wire [5:0] instructiondecode_1_funct, instructiondecode_1_op;
  wire [7:0] wordaddress_1_wordaddress, wordaddress_2_wordaddress;
  wire [15:0] instructiondecode_1_immediate;
  wire [25:0] instructiondecode_1_address;
  wire [31:0] adder_1_out, alu_1_result, branchaddress_1_branchaddress, jumpaddress_1_jumpaddress,
       mips_ram_1_p7, mips_ram_2_p8, multiplexer_2_out, multiplexer_3_out, multiplexer_4_out, register_1_q,
       registerfile_1_p1, registerfile_1_p7, registerfile_1_p8, signextend_1_out_2;

  Register #(.width(32)) register_1 (
    .D(multiplexer_4_out), .Q(register_1_q), .clk(Clock_out), .clr(Reset));  // open: en
  Clock Clock (.out(Clock_out));
  WordAddress wordaddress_1 (.ByteAddress(register_1_q), .WordAddress(wordaddress_1_wordaddress));  // open: Unaligned
  JumpAddress jumpaddress_1 (
    .Address(instructiondecode_1_address), .PC_4(adder_1_out), .JumpAddress(jumpaddress_1_jumpaddress));
  InstructionDecode instructiondecode_1 (
    .Instruction(mips_ram_1_p7), .op(instructiondecode_1_op), .rs(instructiondecode_1_rs),
    .rt(instructiondecode_1_rt), .rd(instructiondecode_1_rd), .funct(instructiondecode_1_funct),
    .immediate(instructiondecode_1_immediate), .address(instructiondecode_1_address));  // open: shamt
  // MIPS_RAM mips_ram_1: pin names not known; wires that end beside it: wordaddress_1_wordaddress, 1'b0, 4'b1111, 1'b0, 1'b1, Clear, mips_ram_1_p7
  Control control_1 (
    .op(instructiondecode_1_op), .Jump(control_1_jump), .RegDst(control_1_regdst), .Branch(control_1_branch),
    .LeMem(control_1_lemem), .MemparaReg(control_1_memparareg), .OpALU(control_1_opalu),
    .EscreveMem(control_1_escrevemem), .OrigALU(control_1_origalu), .EscreveReg(control_1_escrevereg));
  Multiplexer #(.width(5), .enable("false")) multiplexer_1 (
    .in0(instructiondecode_1_rt), .in1(instructiondecode_1_rd), .out(multiplexer_1_out),
    .sel(control_1_regdst));
  Adder #(.width(32)) adder_1 (.a(32'h4), .b(register_1_q), .out(adder_1_out));  // open: cin, cout
  not not_1 (not_1_out, Clock_out);
  SignExtend signextend_1 (.in_1(instructiondecode_1_immediate), .out_2(signextend_1_out_2));
  // RegisterFile registerfile_1: pin names not known; wires that end beside it: registerfile_1_p1, not_1_out, control_1_escrevereg, multiplexer_1_out, instructiondecode_1_rs, instructiondecode_1_rt, registerfile_1_p7, registerfile_1_p8
  Multiplexer #(.width(32), .enable("false")) multiplexer_2 (
    .in0(registerfile_1_p8), .in1(signextend_1_out_2), .out(multiplexer_2_out), .sel(control_1_origalu));
  WordAddress wordaddress_2 (.ByteAddress(alu_1_result), .WordAddress(wordaddress_2_wordaddress));  // open: Unaligned
  BranchAddress branchaddress_1 (
    .PC_4(adder_1_out), .Address(signextend_1_out_2), .BranchAddress(branchaddress_1_branchaddress));
  ALUcontrol alucontrol_1 (
    .funct(instructiondecode_1_funct), .OpALU(control_1_opalu), .Operation(alucontrol_1_operation));
  Multiplexer #(.width(32), .enable("false")) multiplexer_3 (
    .in0(adder_1_out), .in1(branchaddress_1_branchaddress), .out(multiplexer_3_out), .sel(and_1_out));
  and and_1 (and_1_out, control_1_branch, alu_1_zero);
  ALU alu_1 (
    .A(registerfile_1_p7), .B(multiplexer_2_out), .Operation(alucontrol_1_operation), .Zero(alu_1_zero),
    .Result(alu_1_result));  // open: Overflow
  // MIPS_RAM mips_ram_2: pin names not known; wires that end beside it: wordaddress_2_wordaddress, registerfile_1_p8, control_1_escrevemem, 4'b1111, not_1_out, control_1_lemem, Clear_2, mips_ram_2_p8
  Multiplexer #(.width(32), .enable("false")) multiplexer_4 (
    .in0(multiplexer_3_out), .in1(jumpaddress_1_jumpaddress), .out(multiplexer_4_out), .sel(control_1_jump));
  Multiplexer #(.width(32), .enable("false")) multiplexer_5 (
    .in0(alu_1_result), .in1(mips_ram_2_p8), .out(registerfile_1_p1), .sel(control_1_memparareg));

  // Notes on the sheet:
  //   PC
  //   Opcode
  //   Memória de Instruções
  //   Instruções
  //   Decodificador
  //   Controler
  //   Registradores
  //   Extensão
  //   Branch
  //   Controle ALU
  //   Memória de Dados
  //   ALU
endmodule

module Control (
  input  [5:0] op,
  output Jump,
  output RegDst,
  output Branch,
  output LeMem,
  output MemparaReg,
  output [1:0] OpALU,
  output EscreveMem,
  output OrigALU,
  output EscreveReg
);

  wire Addi_out;

  and J (Jump, ~op[0], op[1], ~op[2], ~op[3], ~op[4], ~op[5]);  // AND_Gate
  and R (OpALU[1], ~op[0], ~op[1], ~op[2], ~op[3], ~op[4], ~op[5]);  // AND_Gate
  and lw (LeMem, op[0], op[1], ~op[2], ~op[3], ~op[4], op[5]);  // AND_Gate
  and sw (EscreveMem, op[0], op[1], ~op[2], op[3], ~op[4], op[5]);  // AND_Gate
  and beq (Branch, ~op[0], ~op[1], op[2], ~op[3], ~op[4], ~op[5]);  // AND_Gate
  and Addi (Addi_out, ~op[0], ~op[1], ~op[2], op[3], ~op[4], ~op[5]);  // AND_Gate
  or or_1 (EscreveReg, LeMem, Addi_out, OpALU[1]);
  or or_2 (OrigALU, LeMem, Addi_out, EscreveMem);

  assign MemparaReg = LeMem;
  assign OpALU[0] = Branch;
  assign RegDst = OpALU[1];
endmodule

module ALUcontrol (
  input  [5:0] funct,
  input  [1:0] OpALU,
  output [3:0] Operation
);

  wire and_2_out, or_1_out;

  or or_1 (or_1_out, funct[0], funct[3]);
  and and_1 (Operation[0], or_1_out, OpALU[1]);
  or or_2 (Operation[1], ~funct[2], ~OpALU[1]);  // OR_Gate
  and and_2 (and_2_out, OpALU[1], funct[1]);
  or or_3 (Operation[2], and_2_out, OpALU[0]);

  assign Operation[3] = 1'b0;
endmodule
